# Fritzing sketch message_router_board (saved by Fritzing 0.5.2b)
breadboards: 1

parts:
  Propeller1 = Parallax Propeller D40 [package="DIP [THT]"]
  IC1 = 24LC256 [package=THT]
  10_KOhm = Resistor [resistance=10k package=THT]
  3_3V_Regulator = Voltage Regulator - 3.3V [package="TO220 [THT]"]
  Propeller_Plug = female pin header, 4 pins [form="♀ (female)"]
  5MHz_Ocillator = Crystal
  10uF = Ceramic Capacitor [capacitance=10µF rated_voltage=35V package="100 mil [THT, multilayer]"]
  68_Ohm = Resistor [resistance=68 package=THT]
  LED1 = Red LED - 5mm [package="5 mm [THT]"]
  PROP1_DB9_Female_(PMC_BOARD) = DB9_rt_female
  PROP2_DB9_Female_(VS_BOARD) = DB9_rt_female
  PROP3_DB9_Female = DB9_rt_female
  PROP4_DB9_Female = DB9_rt_female
  XBEE_DB9_Female = DB9_rt_female
  Power_plug_(to_power_/_motor_controller_board_plug_1_for_primary) = Power plug
  3_3V_Regulator_2 = Voltage Regulator - 3.3V [package="TO220 [THT]"]
  Power_plug_(to_power_/_motor_controller_board_plug2_for_xbee) = Power plug

nets (from the schematic view):
  N1: Propeller1.P0, XBEE_DB9_Female.connector6
  N2: Propeller1.P1, XBEE_DB9_Female.connector7
  N3: Propeller1.P2, PROP1_DB9_Female_(PMC_BOARD).connector6
  N4: Propeller1.P3, PROP1_DB9_Female_(PMC_BOARD).connector7
  N5: Propeller1.P4, PROP2_DB9_Female_(VS_BOARD).connector6
  N6: Propeller1.P5, PROP2_DB9_Female_(VS_BOARD).connector7
  N7: Propeller1.P6, PROP3_DB9_Female.connector6
  N8: Propeller1.P7, PROP3_DB9_Female.connector7
  GND: Propeller1.VSS, Propeller1.BOEn, IC1.A0, IC1.A1, IC1.A2, IC1.0V, IC1.WP_-_Write_Protect, 3_3V_Regulator.GND, Propeller_Plug.pin1, 10uF.1, LED1.cathode, PROP1_DB9_Female_(PMC_BOARD).connector8, PROP2_DB9_Female_(VS_BOARD).connector8, PROP3_DB9_Female.connector8, PROP4_DB9_Female.connector8, XBEE_DB9_Female.connector8, Power_plug_(to_power_/_motor_controller_board_plug_1_for_primary).GND, 3_3V_Regulator_2.GND, Power_plug_(to_power_/_motor_controller_board_plug2_for_xbee).GND
  N9: Propeller1.RESn, Propeller_Plug.pin2
  N10: Propeller1.VDD, IC1.+V, 10_KOhm.Pin_1, 3_3V_Regulator.output_voltage, 10uF.0
  N11: Propeller1.P8, PROP4_DB9_Female.connector6
  N12: Propeller1.P9, PROP4_DB9_Female.connector7
  N13: Propeller1.XI, 5MHz_Ocillator.connector1
  N14: Propeller1.XO, 5MHz_Ocillator.connector0
  N15: Propeller1.P27, 68_Ohm.Pin_0
  N16: Propeller1.P28, IC1.SCL_-_I2C_Clock
  N17: Propeller1.P29, IC1.SDA_-_I2C_Data, 10_KOhm.Pin_0
  N18: Propeller1.P30, Propeller_Plug.pin4
  N19: Propeller1.P31, Propeller_Plug.pin3
  N20: 3_3V_Regulator.input_voltage, Power_plug_(to_power_/_motor_controller_board_plug_1_for_primary).VCC
  N21: 68_Ohm.Pin_1, LED1.anode
  N22: XBEE_DB9_Female.connector5, 3_3V_Regulator_2.output_voltage
  N23: 3_3V_Regulator_2.input_voltage, Power_plug_(to_power_/_motor_controller_board_plug2_for_xbee).VCC

notes:
  MESSAGE ROUTER BOARD
