# Fritzing sketch motor_interconnect (saved by Fritzing 0.5.2b)
breadboards: 1

parts:
  MOTOR_2 = female pin header, 6 pins [form="♀ (female)"]
  MOTOR_1 = female pin header, 6 pins [form="♀ (female)"]
  POWER_/_MOTOR_CONTROLLER_BOARD = female pin header, 7 pins [form="♀ (female)"]
  SABERTOOTH_2X5_MOTOR_CONTROLLER = female pin header, 9 pins [form="♀ (female)"]
  To_power_/_motor_controller_board_plug_10 = Power plug

nets:
  N1: MOTOR_2.pin1, SABERTOOTH_2X5_MOTOR_CONTROLLER.pin5
  N2: MOTOR_2.pin2, SABERTOOTH_2X5_MOTOR_CONTROLLER.pin6
  N3: MOTOR_2.pin3, MOTOR_1.pin3, POWER_/_MOTOR_CONTROLLER_BOARD.pin6, SABERTOOTH_2X5_MOTOR_CONTROLLER.pin8
  N4: MOTOR_2.pin4, MOTOR_1.pin4, POWER_/_MOTOR_CONTROLLER_BOARD.pin7, SABERTOOTH_2X5_MOTOR_CONTROLLER.pin9
  N5: MOTOR_2.pin5, POWER_/_MOTOR_CONTROLLER_BOARD.pin4
  N6: MOTOR_2.pin6, POWER_/_MOTOR_CONTROLLER_BOARD.pin5
  N7: MOTOR_1.pin1, SABERTOOTH_2X5_MOTOR_CONTROLLER.pin3
  N8: MOTOR_1.pin2, SABERTOOTH_2X5_MOTOR_CONTROLLER.pin4
  N9: MOTOR_1.pin5, POWER_/_MOTOR_CONTROLLER_BOARD.pin2
  N10: MOTOR_1.pin6, POWER_/_MOTOR_CONTROLLER_BOARD.pin3
  N11: POWER_/_MOTOR_CONTROLLER_BOARD.pin1, SABERTOOTH_2X5_MOTOR_CONTROLLER.pin7
  N12: SABERTOOTH_2X5_MOTOR_CONTROLLER.pin1, To_power_/_motor_controller_board_plug_10.GND
  N13: SABERTOOTH_2X5_MOTOR_CONTROLLER.pin2, To_power_/_motor_controller_board_plug_10.VCC

notes:
  DUAL GEARHEAD MOTORS, SABERTOOTH & POWER / MOTOR CONTROLLER INTERCONNECT
  1 - RS232 Sabertooth
  2 - Motor1 Ch A
  3 - Motor1 Ch B
  4 - Motor2 Ch A
  5 - Motor2 Ch B
  6 - 5V
  7 - GND
  1 - B-
  2 - B+
  3 - M1A
  4 - M1B
  5 - M2A
  6 - M2B
  7 - S1 (RS232 TX from power / motor controller board)
  8 - 5V (Power output @ 100mA)
  9 - 0V (RS232 GND to power / motor controller board)
  * NOTE: Be sure that you have properly set the DIP switch so that we're in SIMPLIFIED SERIAL mode. See the user's manual for details.
  1 - Motor Power Supply Wire: Vcc Power In (0 - 12 volts)
  2 - Motor Power Supply Wire: Gnd Power In
  3 - Encoder Adapter Board Vcc: +5V to 12V
  4 - Encoder Adapter Board Ground
  5 - Encoder Adapter Board Channel A (0v-5v out)
  6 - Encoder Adapter Board Channel B (0v-5v out)
