# Fritzing sketch power_motor_controller_board (saved by Fritzing 0.5.2b)
breadboards: 1

parts:
  Propeller1 = Parallax Propeller D40 [package="DIP [THT]"]
  IC1 = 24LC256 [package=THT]
  10_KOhm = Resistor [resistance=10k package=THT]
  3_3V_Regulator = Voltage Regulator - 3.3V [package="TO220 [THT]"]
  Propeller_Plug = female pin header, 4 pins [form="♀ (female)"]
  (-)_DC_Unregulated_Battery_Power = DC Power [voltage=7.2]
  10uF = Ceramic Capacitor [capacitance=10µF rated_voltage=35V package="100 mil [THT, multilayer]"]
  68_Ohm = Resistor [resistance=68 package=THT]
  LED1 = Red LED - 5mm [package="5 mm [THT]"]
  5_MHz_Ocillator = Crystal
  MESSAGE_ROUTER_DB9_MALE = DB9_Female
  LH1500AT1 = DIP - 6 pins
  LH1500AT2 = DIP - 6 pins
  LH1500AT3 = DIP - 6 pins
  LH1500AT4 = DIP - 6 pins
  LH1500AT5 = DIP - 6 pins
  LH1500AT6 = DIP - 6 pins
  LH1500AT7 = DIP - 6 pins
  LH1500AT8 = DIP - 6 pins
  Power_plug1_(to_message_router_board_primary) = Power plug
  Power_plug2_(to_message_router_board_xbee) = Power plug
  Power_plug3_(to_vision_/_sram_board_primary) = Power plug
  Power_plug_4_(to_vision_/_sram_board_camera) = Power plug
  Power_plug5_(to_vision_/_sram_board_sram_card) = Power plug
  Power_plug6_(to_terminal_sensor_board_primary) = Power plug
  Power_plug7_(to_terminal_sensor_board_sensors) = Power plug
  Power_plug8_(to_storage_sensor_board_primary) = Power plug
  Sparkfun_BOB_08745_Level_Converter1 = DIP - 12 pins
  Sparkfun_BOB_08745_Level_Converter2 = DIP - 12 pins
  To_Motor_Interconnect = female pin header, 7 pins [form="♀ (female)"]
  LH1500AT9 = DIP - 6 pins
  Power_plug9_(to_storage_sensor_board_storage) = Power plug
  LH1500AT10 = DIP - 6 pins
  Power_plug10_(to_motor_interconnect) = Power plug

nets:
  N1: Propeller1.P0, MESSAGE_ROUTER_DB9_MALE.connector6
  N2: Propeller1.P1, MESSAGE_ROUTER_DB9_MALE.connector7
  N3: Propeller1.P2, Sparkfun_BOB_08745_Level_Converter1.connector5
  N4: Propeller1.P3, Sparkfun_BOB_08745_Level_Converter1.connector4
  N5: Propeller1.P4, Sparkfun_BOB_08745_Level_Converter1.connector1
  N6: Propeller1.P5, Sparkfun_BOB_08745_Level_Converter2.connector4
  N7: Propeller1.P6, Sparkfun_BOB_08745_Level_Converter2.connector1
  GND: Propeller1.VSS, Propeller1.BOEn, IC1.A0, IC1.A1, IC1.A2, IC1.0V, IC1.WP_-_Write_Protect, 3_3V_Regulator.GND, Propeller_Plug.pin1, (-)_DC_Unregulated_Battery_Power.GND, 10uF.1, LED1.cathode, MESSAGE_ROUTER_DB9_MALE.connector8, LH1500AT1.connector1, LH1500AT2.connector1, LH1500AT3.connector1, LH1500AT4.connector1, LH1500AT5.connector1, LH1500AT6.connector1, LH1500AT7.connector1, LH1500AT8.connector1, Sparkfun_BOB_08745_Level_Converter1.connector3, Sparkfun_BOB_08745_Level_Converter2.connector3, LH1500AT9.connector1, LH1500AT10.connector1
  N8: Propeller1.RESn, Propeller_Plug.pin2
  N9: Propeller1.VDD, IC1.+V, 10_KOhm.Pin_1, 3_3V_Regulator.output_voltage, 10uF.0, Sparkfun_BOB_08745_Level_Converter1.connector2, Sparkfun_BOB_08745_Level_Converter2.connector2
  N10: Propeller1.P15, LH1500AT10.connector0
  N11: Propeller1.P16, LH1500AT9.connector0
  N12: Propeller1.P17, LH1500AT8.connector0
  N13: Propeller1.P18, LH1500AT7.connector0
  N14: Propeller1.P19, LH1500AT6.connector0
  N15: Propeller1.P20, LH1500AT5.connector0
  N16: Propeller1.P21, LH1500AT4.connector0
  N17: Propeller1.P22, LH1500AT3.connector0
  N18: Propeller1.P23, LH1500AT2.connector0
  N19: Propeller1.XI, 5_MHz_Ocillator.connector1
  N20: Propeller1.XO, 5_MHz_Ocillator.connector0
  N21: Propeller1.P24, LH1500AT1.connector0
  N22: Propeller1.P27, 68_Ohm.Pin_0
  N23: Propeller1.P28, IC1.SCL_-_I2C_Clock
  N24: Propeller1.P29, IC1.SDA_-_I2C_Data, 10_KOhm.Pin_0
  N25: Propeller1.P30, Propeller_Plug.pin4
  N26: Propeller1.P31, Propeller_Plug.pin3
  N27: 3_3V_Regulator.input_voltage, (-)_DC_Unregulated_Battery_Power.V+
  N28: 68_Ohm.Pin_1, LED1.anode
  N29: LH1500AT1.connector4, Power_plug1_(to_message_router_board_primary).VCC
  N30: LH1500AT1.connector5, Power_plug1_(to_message_router_board_primary).GND
  N31: LH1500AT2.connector4, Power_plug2_(to_message_router_board_xbee).VCC
  N32: LH1500AT2.connector5, Power_plug2_(to_message_router_board_xbee).GND
  N33: LH1500AT3.connector4, Power_plug3_(to_vision_/_sram_board_primary).VCC
  N34: LH1500AT3.connector5, Power_plug3_(to_vision_/_sram_board_primary).GND
  N35: LH1500AT4.connector4, Power_plug_4_(to_vision_/_sram_board_camera).VCC
  N36: LH1500AT4.connector5, Power_plug_4_(to_vision_/_sram_board_camera).GND
  N37: LH1500AT5.connector4, Power_plug5_(to_vision_/_sram_board_sram_card).VCC
  N38: LH1500AT5.connector5, Power_plug5_(to_vision_/_sram_board_sram_card).GND
  N39: LH1500AT6.connector4, Power_plug6_(to_terminal_sensor_board_primary).VCC
  N40: LH1500AT6.connector5, Power_plug6_(to_terminal_sensor_board_primary).GND
  N41: LH1500AT7.connector4, Power_plug7_(to_terminal_sensor_board_sensors).VCC
  N42: LH1500AT7.connector5, Power_plug7_(to_terminal_sensor_board_sensors).GND
  N43: LH1500AT8.connector4, Power_plug8_(to_storage_sensor_board_primary).VCC
  N44: LH1500AT8.connector5, Power_plug8_(to_storage_sensor_board_primary).GND
  N45: Sparkfun_BOB_08745_Level_Converter1.connector6, To_Motor_Interconnect.pin1
  N46: Sparkfun_BOB_08745_Level_Converter1.connector7, To_Motor_Interconnect.pin2
  N47: Sparkfun_BOB_08745_Level_Converter1.connector8, Sparkfun_BOB_08745_Level_Converter2.connector8, To_Motor_Interconnect.pin6
  N48: Sparkfun_BOB_08745_Level_Converter1.connector9, Sparkfun_BOB_08745_Level_Converter2.connector9, To_Motor_Interconnect.pin7
  N49: Sparkfun_BOB_08745_Level_Converter1.connector10, To_Motor_Interconnect.pin3
  N50: Sparkfun_BOB_08745_Level_Converter2.connector7, To_Motor_Interconnect.pin4
  N51: Sparkfun_BOB_08745_Level_Converter2.connector10, To_Motor_Interconnect.pin5
  N52: LH1500AT9.connector4, Power_plug9_(to_storage_sensor_board_storage).VCC
  N53: LH1500AT9.connector5, Power_plug9_(to_storage_sensor_board_storage).GND
  N54: LH1500AT10.connector4, Power_plug10_(to_motor_interconnect).VCC
  N55: LH1500AT10.connector5, Power_plug10_(to_motor_interconnect).GND

notes:
  POWER / MOTOR CONTROLLER BOARD
  Connections from the top:
  1 - RS232 Sabertooth
  2 - Motor1 Ch A
  3 - Motor1 Ch B
  4 - Motor2 Ch A
  5 - Motor2 Ch B
  6 - +5V
  7 - GND
