# Fritzing sketch storage_sensor_board (saved by Fritzing 0.5.2b)
breadboards: 1

parts:
  Propeller1 = Parallax Propeller D40 [package="DIP [THT]"]
  IC1 = 24LC256 [package=THT]
  10_KOhm = Resistor [resistance=10k package=THT]
  3_3V_Regulator = Voltage Regulator - 3.3V [package="TO220 [THT]"]
  Propeller_Plug = female pin header, 4 pins [form="♀ (female)"]
  10uF = Ceramic Capacitor [capacitance=10µF rated_voltage=35V package="100 mil [THT, multilayer]"]
  68_Ohm = Resistor [resistance=68 package=THT]
  LED1 = Red LED - 5mm [package="5 mm [THT]"]
  5_MHz_Ocillator = Crystal
  Message_Router_DB9_Male = DB9_Female
  Power_plug_(to_power_/_motor_controller_board_plug_8) = Power plug
  3_3V_Regulator_2 = Voltage Regulator - 3.3V [package="TO220 [THT]"]
  Power_plug_(to_power_/_motor_controller_board_plug_9) = Power plug

nets (from the schematic view):
  N1: Propeller1.P0, Message_Router_DB9_Male.connector6
  N2: Propeller1.P1, Message_Router_DB9_Male.connector7
  GND: Propeller1.VSS, Propeller1.BOEn, IC1.A0, IC1.A1, IC1.A2, IC1.0V, IC1.WP_-_Write_Protect, 3_3V_Regulator.GND, Propeller_Plug.pin1, 10uF.1, LED1.cathode, Message_Router_DB9_Male.connector8, Power_plug_(to_power_/_motor_controller_board_plug_8).GND
  N3: Propeller1.RESn, Propeller_Plug.pin2
  N4: Propeller1.VDD, IC1.+V, 10_KOhm.Pin_1, 3_3V_Regulator.output_voltage, 10uF.0
  N5: Propeller1.XI, 5_MHz_Ocillator.connector1
  N6: Propeller1.XO, 5_MHz_Ocillator.connector0
  N7: Propeller1.P27, 68_Ohm.Pin_0
  N8: Propeller1.P28, IC1.SCL_-_I2C_Clock
  N9: Propeller1.P29, IC1.SDA_-_I2C_Data, 10_KOhm.Pin_0
  N10: Propeller1.P30, Propeller_Plug.pin4
  N11: Propeller1.P31, Propeller_Plug.pin3
  N12: 3_3V_Regulator.input_voltage, Power_plug_(to_power_/_motor_controller_board_plug_8).VCC
  N13: 3_3V_Regulator_2.input_voltage, Power_plug_(to_power_/_motor_controller_board_plug_9).VCC

notes:
  STORAGE SENSOR BOARD
