# Fritzing sketch terminal_sensor_board (saved by Fritzing 0.5.2b)
breadboards: 1

parts:
  Propeller1 = Parallax Propeller D40 [package="DIP [THT]"]
  IC1 = 24LC256 [package=THT]
  10_KOhm = Resistor [resistance=10k package=THT]
  3_3V_Regulator = Voltage Regulator - 3.3V [package="TO220 [THT]"]
  Propeller_Plug = female pin header, 4 pins [form="♀ (female)"]
  10uF = Ceramic Capacitor [capacitance=10µF rated_voltage=35V package="100 mil [THT, multilayer]"]
  68_Ohm = Resistor [resistance=68 package=THT]
  LED1 = Red LED - 5mm [package="5 mm [THT]"]
  5_MHz_Ocillator = Crystal
  Message_Router_DB9_Male = DB9_Female
  Power_plug_(to_pmc_board_plug_6) = Power plug
  5V_Regulator = Voltage Regulator - 3.3V [package="TO220 [THT]"]
  Power_plug_(to_power_/_motor_controller_board_plug_7) = Power plug
  MCP32081 = DIP - 16 pins
  SHARP_2Y0A21 = female pin header, 3 pins [form="♀ (female)"]
  SHARP_2Y0A02 = female pin header, 3 pins [form="♀ (female)"]
  PARALLAX_LCD_TERMINAL_APPMOD = female pin header, 20 pins [form="♀ (female)"]
  POT1_(adjust_to_2_55V) = Trimmer Potentiometer [package=THT]
  1_kOhm = Resistor [resistance=1k package=THT]
  HYGROMETER = female pin header, 2 pins [form="♀ (female)"]
  4_7_kOhm = Resistor [resistance=1k package=THT]
  4_7_kOhm_2 = Resistor [resistance=1k package=THT]
  4_7_kOhm_3 = Resistor [resistance=1k package=THT]
  4_7_kOhm_4 = Resistor [resistance=1k package=THT]
  4_7_kOhm_5 = Resistor [resistance=1k package=THT]
  4_7_kOhm_6 = Resistor [resistance=1k package=THT]
  4_7_kOhm_7 = Resistor [resistance=1k package=THT]
  4_7_kOhm_8 = Resistor [resistance=1k package=THT]

nets (from the schematic view):
  N1: Propeller1.P0, Message_Router_DB9_Male.connector6
  N2: Propeller1.P1, Message_Router_DB9_Male.connector7
  GND: Propeller1.VSS, Propeller1.BOEn, IC1.A0, IC1.A1, IC1.A2, IC1.0V, IC1.WP_-_Write_Protect, 3_3V_Regulator.GND, Propeller_Plug.pin1, 10uF.1, LED1.cathode, Message_Router_DB9_Male.connector8, Power_plug_(to_pmc_board_plug_6).GND, PARALLAX_LCD_TERMINAL_APPMOD.pin10, PARALLAX_LCD_TERMINAL_APPMOD.pin11
  N3: Propeller1.RESn, Propeller_Plug.pin2
  N4: Propeller1.VDD, IC1.+V, 10_KOhm.Pin_1, 3_3V_Regulator.output_voltage, 10uF.0
  N5: Propeller1.P13, MCP32081.connector12
  N6: Propeller1.P14, 1_kOhm.Pin_0
  N7: Propeller1.P15, MCP32081.connector9
  N8: Propeller1.P16, 4_7_kOhm_8.Pin_1
  N9: Propeller1.P17, 4_7_kOhm_5.Pin_1
  N10: Propeller1.P18, 4_7_kOhm_4.Pin_1
  N11: Propeller1.P19, 4_7_kOhm.Pin_1
  N12: Propeller1.P20, 4_7_kOhm_2.Pin_1
  N13: Propeller1.P21, 4_7_kOhm_3.Pin_1
  N14: Propeller1.P22, 4_7_kOhm_6.Pin_1
  N15: Propeller1.P23, 4_7_kOhm_7.Pin_1
  N16: Propeller1.XI, 5_MHz_Ocillator.connector1
  N17: Propeller1.XO, 5_MHz_Ocillator.connector0
  N18: Propeller1.P27, 68_Ohm.Pin_0
  N19: Propeller1.P28, IC1.SCL_-_I2C_Clock
  N20: Propeller1.P29, IC1.SDA_-_I2C_Data, 10_KOhm.Pin_0
  N21: Propeller1.P30, Propeller_Plug.pin4
  N22: Propeller1.P31, Propeller_Plug.pin3
  N23: 3_3V_Regulator.input_voltage, Power_plug_(to_pmc_board_plug_6).VCC
  N24: 5V_Regulator.input_voltage, Power_plug_(to_power_/_motor_controller_board_plug_7).VCC
  GND_2: 5V_Regulator.GND, Power_plug_(to_power_/_motor_controller_board_plug_7).GND
  N25: 5V_Regulator.output_voltage, MCP32081.connector15, SHARP_2Y0A21.pin3, SHARP_2Y0A02.pin3, PARALLAX_LCD_TERMINAL_APPMOD.pin1, POT1_(adjust_to_2_55V).leg2
  N26: MCP32081.connector0, SHARP_2Y0A02.pin1
  N27: MCP32081.connector1, SHARP_2Y0A21.pin1
  N28: MCP32081.connector2, HYGROMETER.pin1
  N29: MCP32081.connector8, MCP32081.connector13, SHARP_2Y0A21.pin2, SHARP_2Y0A02.pin2, HYGROMETER.pin2
  N30: MCP32081.connector10, MCP32081.connector11, 1_kOhm.Pin_1
  N31: MCP32081.connector14, POT1_(adjust_to_2_55V).leg1
  N32: PARALLAX_LCD_TERMINAL_APPMOD.pin6, 4_7_kOhm_6.Pin_0
  N33: PARALLAX_LCD_TERMINAL_APPMOD.pin7, 4_7_kOhm_2.Pin_0
  N34: PARALLAX_LCD_TERMINAL_APPMOD.pin8, 4_7_kOhm_4.Pin_0
  N35: PARALLAX_LCD_TERMINAL_APPMOD.pin9, 4_7_kOhm_8.Pin_0
  N36: PARALLAX_LCD_TERMINAL_APPMOD.pin12, 4_7_kOhm_5.Pin_0
  N37: PARALLAX_LCD_TERMINAL_APPMOD.pin13, 4_7_kOhm.Pin_0
  N38: PARALLAX_LCD_TERMINAL_APPMOD.pin14, 4_7_kOhm_3.Pin_0
  N39: PARALLAX_LCD_TERMINAL_APPMOD.pin15, 4_7_kOhm_7.Pin_0

notes:
  TERMINAL SENSOR BOARD
  1 - Vo - Voltage Output
  2 - GND - Ground
  3 - Vcc - SUpply Voltage
  1 - VDD
  2 - P14 (UNUSED)
  3 - P12 (UNUSED)
  4 - P10 (UNUSED)
  5 - P8 (UNUSED)
  6 - P6
  7 - P4
  8 - P2
  9 - P0
  10 - VSS
  11 - VSS
  12 - P1
  13 - P3
  14 - P5
  15 - P7
  16 - P9 (UNUSED)
  17 - P11 (UNUSED)
  18 - P13 (UNUSED)
  19 - P16 (UNUSED)
  20 - VIN (UNUSED)
  ** This is counting clockwise based on the diagram in the datasheet
  1 - Vo - Voltage Output
  2 - GND - Ground
