# Fritzing sketch vision_sram_board (saved by Fritzing 0.5.2b)
breadboards: 1

parts:
  Propeller1 = Parallax Propeller D40 [package="DIP [THT]"]
  IC1 = 24LC256 [package=THT]
  10_KOhm = Resistor [resistance=10k package=THT]
  3_3V_Regulator = Voltage Regulator - 3.3V [package="TO220 [THT]"]
  Propeller_Plug = female pin header, 4 pins [form="♀ (female)"]
  10uF = Ceramic Capacitor [capacitance=10µF rated_voltage=35V package="100 mil [THT, multilayer]"]
  68_Ohm = Resistor [resistance=68 package=THT]
  LED1 = Red LED - 5mm [package="5 mm [THT]"]
  5_MHz_Ocillator = Crystal
  Message_Router_DB9_Male = DB9_Female
  Power_plug_(to_pmc_board_to_plug_2) = Power plug
  Linksprite_LS-201_JPEG_Color_Camera = female pin header, 4 pins [form="♀ (female)"]
  68_Ohm_2 = Resistor [resistance=68 package=THT]
  68_Ohm_3 = Resistor [resistance=68 package=THT]
  Hydra_20_Pin_Cardedge_Female_Connector1 = Generic female header - 20 pins [form="♀ (female)"]
  3_3V_Regulator_2 = Voltage Regulator - 3.3V [package="TO220 [THT]"]
  Power_plug_(to_pmc_board_to_plug_3) = Power plug
  3_3V_Regulator_3 = Voltage Regulator - 3.3V [package="TO220 [THT]"]
  Power_plug_(to_pmc_board_to_plug_4) = Power plug

nets:
  N1: Propeller1.P0, Message_Router_DB9_Male.connector6
  N2: Propeller1.P1, Message_Router_DB9_Male.connector7
  N3: Propeller1.P2, 68_Ohm_2.Pin_1
  N4: Propeller1.P3, 68_Ohm_3.Pin_1
  GND: Propeller1.VSS, Propeller1.BOEn, IC1.A0, IC1.A1, IC1.A2, IC1.0V, IC1.WP_-_Write_Protect, 3_3V_Regulator.GND, 10uF.1, LED1.cathode, Message_Router_DB9_Male.connector8, Power_plug_(to_pmc_board_to_plug_2).GND
  N5: Propeller1.VDD, IC1.+V, 10_KOhm.Pin_1, 3_3V_Regulator.output_voltage, 10uF.0
  N6: Propeller1.P16, Hydra_20_Pin_Cardedge_Female_Connector1.connector0
  N7: Propeller1.P17, Hydra_20_Pin_Cardedge_Female_Connector1.connector1
  N8: Propeller1.P18, Hydra_20_Pin_Cardedge_Female_Connector1.connector2
  N9: Propeller1.P19, Hydra_20_Pin_Cardedge_Female_Connector1.connector3
  N10: Propeller1.P20, Hydra_20_Pin_Cardedge_Female_Connector1.connector4
  N11: Propeller1.P21, Hydra_20_Pin_Cardedge_Female_Connector1.connector5
  N12: Propeller1.P22, Hydra_20_Pin_Cardedge_Female_Connector1.connector6
  N13: Propeller1.P23, Hydra_20_Pin_Cardedge_Female_Connector1.connector7
  N14: Propeller1.XI, 5_MHz_Ocillator.connector1
  N15: Propeller1.XO, 5_MHz_Ocillator.connector0
  N16: Propeller1.P24, Hydra_20_Pin_Cardedge_Female_Connector1.connector8
  N17: Propeller1.P25, Hydra_20_Pin_Cardedge_Female_Connector1.connector9
  N18: Propeller1.P26, Hydra_20_Pin_Cardedge_Female_Connector1.connector10
  N19: Propeller1.P27, 68_Ohm.Pin_0
  N20: Propeller1.P28, IC1.SCL_-_I2C_Clock
  N21: Propeller1.P29, IC1.SDA_-_I2C_Data, 10_KOhm.Pin_0
  N22: Propeller1.P30, Propeller_Plug.pin4, Hydra_20_Pin_Cardedge_Female_Connector1.connector18
  N23: 3_3V_Regulator.input_voltage, Power_plug_(to_pmc_board_to_plug_2).VCC
  N24: 68_Ohm.Pin_1, LED1.anode
  N25: Linksprite_LS-201_JPEG_Color_Camera.pin1, 3_3V_Regulator_3.output_voltage
  GND_2: Linksprite_LS-201_JPEG_Color_Camera.pin2, 3_3V_Regulator_3.GND, Power_plug_(to_pmc_board_to_plug_4).GND
  N26: Linksprite_LS-201_JPEG_Color_Camera.pin3, 68_Ohm_3.Pin_0
  N27: Linksprite_LS-201_JPEG_Color_Camera.pin4, 68_Ohm_2.Pin_0
  N28: Hydra_20_Pin_Cardedge_Female_Connector1.connector13, 3_3V_Regulator_2.output_voltage
  GND_3: Hydra_20_Pin_Cardedge_Female_Connector1.connector19, 3_3V_Regulator_2.GND, Power_plug_(to_pmc_board_to_plug_3).GND
  N29: 3_3V_Regulator_2.input_voltage, Power_plug_(to_pmc_board_to_plug_3).VCC
  N30: 3_3V_Regulator_3.input_voltage, Power_plug_(to_pmc_board_to_plug_4).VCC

notes:
  VISION / SRAM BOARD
  4 - RXD (IN) RS232 level connected to MCU or PC TXD3 - TXD (OUT) RS232 level connected to MCU or PC RXD
  2 - GND Ground
  1 - +5V Power (or 3.3V, as we do in this application)
  (100 mA load)
  20 -GND
  19 - USB_RXD SRAM_CLK (clock strobe)
  14 - 3.3V VCC
  11 - RESn SRAM_RESn (reset)
  10 - NET_RX_CLK SRAM_C0 (control)
  9 - NET_TX_DATA SRAM_C1 (control)
  1..8 - IO_0..IO_7 SRAM_D0..SRAM_D7 (data bus)
