# Fritzing sketch device (saved by Fritzing 0.6.4b)
breadboards: 1

parts:
  LH1500AT1 = LH1500AT_Solid_State_Relay_DIP_6
  LH1500AT2 = LH1500AT_Solid_State_Relay_DIP_6
  Maxim_DS18B20_Programmable_Resolution_1-Wire_Digital_Thermometer1 = Maxim___Dallas_18B20_Temperature_Sensor [part_number="DS18B20\r"]
  Maxim_DS18B20_Programmable_Resolution_1-Wire_Digital_Thermometer2 = Maxim___Dallas_18B20_Temperature_Sensor [part_number="DS18B20\r"]
  Maxim_DS18B20_Programmable_Resolution_1-Wire_Digital_Thermometer3 = Maxim___Dallas_18B20_Temperature_Sensor [part_number="DS18B20\r"]
  Maxim_DS18B20_Programmable_Resolution_1-Wire_Digital_Thermometer4 = Maxim___Dallas_18B20_Temperature_Sensor [part_number="DS18B20\r"]
  Maxim_DS18B20_Programmable_Resolution_1-Wire_Digital_Thermometer5 = Maxim___Dallas_18B20_Temperature_Sensor [part_number="DS18B20\r"]
  P8X32A_QuickStart_Parallax_Propeller1 = P8X32A_QuickStart [part_number=40000]
  U1 = Voltage Regulator - 5V [package="TO220 [THT]"]
  Power_plug1_-_13_8V = Power plug
  M1_Water_Pump = DC Motor
  R1_Water_Heater = Resistor [tolerance=±5% resistance=220 package="1206 [SMD]"]

nets:
  N1: LH1500AT1.connector0, P8X32A_QuickStart_Parallax_Propeller1.connector14
  GND: LH1500AT1.connector1, LH1500AT2.connector1, Maxim_DS18B20_Programmable_Resolution_1-Wire_Digital_Thermometer1.connector3, Maxim_DS18B20_Programmable_Resolution_1-Wire_Digital_Thermometer2.connector3, Maxim_DS18B20_Programmable_Resolution_1-Wire_Digital_Thermometer3.connector3, Maxim_DS18B20_Programmable_Resolution_1-Wire_Digital_Thermometer4.connector3, Maxim_DS18B20_Programmable_Resolution_1-Wire_Digital_Thermometer5.connector3, P8X32A_QuickStart_Parallax_Propeller1.connector18, U1.GND, Power_plug1_-_13_8V.GND, M1_Water_Pump.pin_1, R1_Water_Heater.Pin_0
  N2: LH1500AT1.connector3, M1_Water_Pump.pin_2
  N3: LH1500AT1.connector5, P8X32A_QuickStart_Parallax_Propeller1.connector19, U1.output_voltage
  N4: LH1500AT2.connector0, P8X32A_QuickStart_Parallax_Propeller1.connector13
  N5: LH1500AT2.connector3, R1_Water_Heater.Pin_1
  N6: LH1500AT2.connector5, U1.input_voltage, Power_plug1_-_13_8V.VCC
  N7: Maxim_DS18B20_Programmable_Resolution_1-Wire_Digital_Thermometer1.connector4, P8X32A_QuickStart_Parallax_Propeller1.connector12
  N8: Maxim_DS18B20_Programmable_Resolution_1-Wire_Digital_Thermometer1.connector5, Maxim_DS18B20_Programmable_Resolution_1-Wire_Digital_Thermometer2.connector5, Maxim_DS18B20_Programmable_Resolution_1-Wire_Digital_Thermometer3.connector5, Maxim_DS18B20_Programmable_Resolution_1-Wire_Digital_Thermometer4.connector5, Maxim_DS18B20_Programmable_Resolution_1-Wire_Digital_Thermometer5.connector5, P8X32A_QuickStart_Parallax_Propeller1.connector17
  N9: Maxim_DS18B20_Programmable_Resolution_1-Wire_Digital_Thermometer2.connector4, P8X32A_QuickStart_Parallax_Propeller1.connector11
  N10: Maxim_DS18B20_Programmable_Resolution_1-Wire_Digital_Thermometer3.connector4, P8X32A_QuickStart_Parallax_Propeller1.connector10
  N11: Maxim_DS18B20_Programmable_Resolution_1-Wire_Digital_Thermometer4.connector4, P8X32A_QuickStart_Parallax_Propeller1.connector9
  N12: Maxim_DS18B20_Programmable_Resolution_1-Wire_Digital_Thermometer5.connector4, P8X32A_QuickStart_Parallax_Propeller1.connector8
