# Fritzing sketch device (saved by Fritzing 0.6.4b)
breadboards: 1

parts:
  K2 = LH1500AT_Solid_State_Relay_DIP_6 [package="DIP (Dual Inline) [THT]"]
  K1 = LH1500AT_Solid_State_Relay_DIP_6 [package="DIP (Dual Inline) [THT]"]
  TS5 = Maxim / Dallas 18B20 Temperature Sensor [part_number="DS18B20\r" package="TO92 [THT]"]
  TS4 = Maxim / Dallas 18B20 Temperature Sensor [part_number="DS18B20\r" package="TO92 [THT]"]
  TS3 = Maxim / Dallas 18B20 Temperature Sensor [part_number="DS18B20\r" package="TO92 [THT]"]
  TS2 = Maxim / Dallas 18B20 Temperature Sensor [part_number="DS18B20\r" package="TO92 [THT]"]
  TS1 = Maxim / Dallas 18B20 Temperature Sensor [part_number="DS18B20\r" package="TO92 [THT]"]
  U1 = Voltage Regulator - 5V [package="TO220 [THT]"]
  PP1 = Power plug
  WP1 = DC Motor
  R1 = Resistor [tolerance=±5% resistance=220 package="1206 [SMD]"]
  QSP1 = P8X32A QuickStart [part_number=40000]
  U2 = Voltage Regulator - 5V [package="TO220 [THT]"]
  U3 = Voltage Regulator - 5V [package="TO220 [THT]"]
  U4 = Voltage Regulator - 5V [package="TO220 [THT]"]
  C1 = Ceramic Capacitor [capacitance=10µF voltage=20V package="100 mil [THT, multilayer]"]
  R2 = Resistor [tolerance=±5% resistance=4.7k package=THT]
  R3 = Resistor [tolerance=±5% resistance=4.7k package=THT]
  R4 = Resistor [tolerance=±5% resistance=4.7k package=THT]
  R5 = Resistor [tolerance=±5% resistance=4.7k package=THT]
  R6 = Resistor [tolerance=±5% resistance=4.7k package=THT]

nets:
  N1: K2.anode(+), QSP1.J1_15
  GND: K2.cathode(-), K1.cathode(-), TS5.GND, TS4.GND, TS3.GND, TS2.GND, TS1.GND, U1.GND, PP1.GND, WP1.pin_1, R1.Pin_0, QSP1.J1_39, U2.GND, U3.GND, U4.GND, C1.1
  N2: K2.S', WP1.pin_2
  N3: K2.S, U1.output_voltage, QSP1.J1_40, U2.output_voltage, U3.output_voltage, U4.output_voltage
  N4: K1.anode(+), QSP1.J1_14
  N5: K1.S', R1.Pin_1
  N6: K1.S, U1.input_voltage, PP1.VCC, U2.input_voltage, U3.input_voltage, U4.input_voltage, C1.0
  N7: TS5.DQ, QSP1.J1_13, R6.Pin_0
  VDD: TS5.Vdd, TS4.Vdd, TS3.Vdd, TS2.Vdd, TS1.Vdd, QSP1.J1_38, R2.Pin_1, R3.Pin_1, R4.Pin_1, R5.Pin_1, R6.Pin_1
  N8: TS4.DQ, QSP1.J1_12, R5.Pin_0
  N9: TS3.DQ, QSP1.J1_11, R4.Pin_0
  N10: TS2.DQ, QSP1.J1_10, R3.Pin_0
  N11: TS1.DQ, QSP1.J1_9, R2.Pin_0

custom parts:
  LH1500AT_Solid_State_Relay_DIP_6: The LH1500 is robust, ideal for telecom and ground fault applications. It is an SPST normally open switch (1 form A) that replaces electromechanical relays in many applications. It is constructed using a GaAIAs LED for actuation control and an integrated monolithic die for the switch output. The die, fabricated in a high-voltage dielectrically isolated technology, is comprised of a photodiode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
  Maxim / Dallas 18B20 Temperature Sensor: The DS18B20 digital thermometer provides 9-bit to 12-bit Celsius temperature measurements and has an alarm function with nonvolatile userprogrammable upper and lower trigger points. The DS18B20 communicates over a 1-Wire bus that by definition requires only one data line (and ground) for communication with a central microprocessor. It has an operating temperature range of -55°C to +125°C and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
  P8X32A QuickStart: The QuickStart is an evaluation board for the Propeller. As an open-source reference design the QuickStart board provides basic Propeller circuitry. Developers may use our PCB layout files as their own to speed their project towards completion. As a project board the QuickStart is fully expandable and provides unimpeded access to all I/O pins through an expansion header but includes some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
